// Logisim project Exp-2 Circuit.circ as structural Verilog: 1 circuit, main circuit main
module main (
  input  A,
  input  B,
  input  C,
  input  D,
  input  E,
  input  F,
  output out_7
);

  wire AB_out, ABC_out, ABCD_out, ABCDE_out;

  and AB (AB_out, A, B);
  and ABC (ABC_out, AB_out, C);
  and ABCD (ABCD_out, ABC_out, D);
  and ABCDE (ABCDE_out, ABCD_out, E);
  and ABCDEF (out_7, ABCDE_out, F);

  // Notes on the sheet:
  //   Md. Rifat Ahmed - 1931725042
endmodule
