// Logisim project Exp-3 Circuit.circ as structural Verilog: 1 circuit, main circuit main
module main (
  input  A,
  input  B,
  input  C,
  output out_4
);

  wire A_prime_C_AB_prime_out, A_prime_C_out, AB_prime_out, BC_out, not_1_out, not_2_out;

  not not_1 (not_1_out, A);
  not not_2 (not_2_out, B);
  and A_prime_C (A_prime_C_out, not_1_out, C);
  and AB_prime (AB_prime_out, A, not_2_out);
  and BC (BC_out, B, C);
  or A_prime_C_AB_prime (A_prime_C_AB_prime_out, A_prime_C_out, AB_prime_out);
  or F (out_4, A_prime_C_AB_prime_out, BC_out);

  // Notes on the sheet:
  //   Md. Rifat Ahmed - 1931725042
endmodule
