// Logisim project Circuit Part 1.circ as structural Verilog: 1 circuit, main circuit main
module main (
  input  A,
  input  B,
  input  C,
  output out_4
);

  wire AC__prime_2_out, AC__prime_out, AC_out, BC_prime__prime_2_out, BC_prime__prime_out, BC_prime_out,
       C_prime_out;

  nand C_prime (C_prime_out, C, C);
  nand AC__prime (AC__prime_out, A, C);
  nand BC_prime__prime (BC_prime__prime_out, B, C_prime_out);
  nand AC (AC_out, AC__prime_out, AC__prime_out);
  nand BC_prime (BC_prime_out, BC_prime__prime_out, BC_prime__prime_out);
  nand AC__prime_2 (AC__prime_2_out, AC_out, AC_out);
  nand BC_prime__prime_2 (BC_prime__prime_2_out, BC_prime_out, BC_prime_out);
  nand F (out_4, AC__prime_2_out, BC_prime__prime_2_out);

  // Notes on the sheet:
  //   Md. Rifat Ahmed - 1931725042
endmodule
