// Logisim project XOR, XNOR by NAND.circ as structural Verilog: 1 circuit, main circuit main
module main (
  input  A,
  input  B,
  input  A_2,
  input  B_2,
  output out_5,
  output out_6
);

  wire A_prime_2_out, A_prime_B__prime_2_out, A_prime_B__prime_out, A_prime_B_AB_prime_2_out, A_prime_out,
       AB_prime__prime_2_out, AB_prime__prime_out, B_prime_2_out, B_prime_out;

  nand A_prime (A_prime_out, A, A);
  nand A_prime_2 (A_prime_2_out, A_2, A_2);
  nand B_prime (B_prime_out, B, B);
  nand B_prime_2 (B_prime_2_out, B_2, B_2);
  nand A_prime_B__prime (A_prime_B__prime_out, A_prime_out, B);
  nand AB_prime__prime (AB_prime__prime_out, A, B_prime_out);
  nand A_prime_B__prime_2 (A_prime_B__prime_2_out, A_prime_2_out, B_2);
  nand AB_prime__prime_2 (AB_prime__prime_2_out, A_2, B_prime_2_out);
  nand A_prime_B_AB_prime (out_5, A_prime_B__prime_out, AB_prime__prime_out);
  nand A_prime_B_AB_prime_2 (A_prime_B_AB_prime_2_out, A_prime_B__prime_2_out, AB_prime__prime_2_out);
  nand A_prime_B_prime_AB (out_6, A_prime_B_AB_prime_2_out, A_prime_B_AB_prime_2_out);

  // Notes on the sheet:
  //   Md. Rifat Ahmed
  //   ID: 1931725042
  //   Md. Rifat Ahmed
  //   ID: 1931725042
endmodule
