// Logisim project XOR, XNOR by NOR.circ as structural Verilog: 1 circuit, main circuit main
module main (
  input  A,
  input  B,
  input  A_2,
  input  B_2,
  output out_5,
  output out_6
);

  wire A_B__prime_2_out, A_B__prime_out, A_prime_2_out, A_prime_B_AB_prime_2_out,
       A_prime_B_prime__prime_2_out, A_prime_B_prime__prime_out, A_prime_out, B_prime_2_out, B_prime_out;

  nor A_prime (A_prime_out, A, A);
  nor A_prime_2 (A_prime_2_out, A_2, A_2);
  nor B_prime (B_prime_out, B, B);
  nor B_prime_2 (B_prime_2_out, B_2, B_2);
  nor A_B__prime (A_B__prime_out, A, B);
  nor A_prime_B_prime__prime (A_prime_B_prime__prime_out, A_prime_out, B_prime_out);
  nor A_B__prime_2 (A_B__prime_2_out, A_2, B_2);
  nor A_prime_B_prime__prime_2 (A_prime_B_prime__prime_2_out, A_prime_2_out, B_prime_2_out);
  nor A_prime_B_AB_prime (out_5, A_B__prime_out, A_prime_B_prime__prime_out);
  nor A_prime_B_AB_prime_2 (A_prime_B_AB_prime_2_out, A_B__prime_2_out, A_prime_B_prime__prime_2_out);
  nor A_prime_B_prime_AB (out_6, A_prime_B_AB_prime_2_out, A_prime_B_AB_prime_2_out);

  // Notes on the sheet:
  //   Md. Rifat Ahmed
  //   ID: 1931725042
  //   Md. Rifat Ahmed
  //   ID: 1931725042
endmodule
