// Logisim project Circuit 1.circ as structural Verilog: 1 circuit, main circuit main
module main (
  input  A,
  input  B,
  input  C,
  output out_4
);

  wire A_prime_B_prime_C_out, A_prime_BC_prime_out, ABC_prime_out, not_1_out, not_2_out, not_3_out;

  not not_1 (not_1_out, A);
  not not_2 (not_2_out, C);
  not not_3 (not_3_out, B);
  and A_prime_B_prime_C (A_prime_B_prime_C_out, not_1_out, not_3_out, C);
  and A_prime_BC_prime (A_prime_BC_prime_out, not_1_out, B, not_2_out);
  and ABC_prime (ABC_prime_out, A, B, not_2_out);
  or F (out_4, A_prime_B_prime_C_out, A_prime_BC_prime_out, ABC_prime_out);

  // Notes on the sheet:
  //   Md. Rifat Ahmed
  //   ID: 1931725042
endmodule
