// Logisim project Circuit 2.circ as structural Verilog: 1 circuit, main circuit main
module main (
  input  A,
  input  B,
  input  C,
  output out_4
);

  wire A_B_C_out, A_B_prime_C_prime_out, A_prime_B_C_out, A_prime_B_C_prime_out, A_prime_B_prime_C_prime_out,
       and_1_out, not_1_out, not_2_out, not_3_out;

  not not_1 (not_1_out, A);
  not not_2 (not_2_out, B);
  not not_3 (not_3_out, C);
  or A_B_C (A_B_C_out, A, B, C);
  or A_B_prime_C_prime (A_B_prime_C_prime_out, A, not_2_out, not_3_out);
  or A_prime_B_C (A_prime_B_C_out, not_1_out, B, C);
  or A_prime_B_C_prime (A_prime_B_C_prime_out, not_1_out, B, not_3_out);
  or A_prime_B_prime_C_prime (A_prime_B_prime_C_prime_out, not_1_out, not_2_out, not_3_out);
  and and_1 (and_1_out, A_B_C_out, A_B_prime_C_prime_out, A_prime_B_C_out);
  and F (out_4, and_1_out, A_prime_B_C_prime_out, A_prime_B_prime_C_prime_out);

  // Notes on the sheet:
  //   Md. Rifat Ahmed
  //   ID: 1931725042
endmodule
