// Logisim project Circuit 2.circ as structural Verilog: 1 circuit, main circuit main
module main (
  input  W,
  input  X,
  input  Y,
  input  Z,
  output [3:0] out_5
);

  wire nand_1_out, nand_2_out, nand_4_out, nand_5_out, nand_6_out, nand_7_out, nand_8_out, nand_9_out,
       nand_10_out, nand_11_out, nand_12_out, nand_13_out, nand_14_out, nand_15_out;

  nand nand_1 (nand_1_out, X, X);
  nand nand_2 (nand_2_out, Y, Y);
  nand nand_3 (out_5[0], Z, Z);
  nand nand_4 (nand_4_out, X, Z);
  nand nand_5 (nand_5_out, X, Y);
  nand nand_6 (nand_6_out, nand_1_out, Z);
  nand nand_7 (nand_7_out, nand_1_out, Y);
  nand nand_8 (nand_8_out, X, nand_2_out, out_5[0]);
  nand nand_9 (nand_9_out, nand_2_out, out_5[0]);
  nand nand_10 (nand_10_out, Y, Z);
  nand nand_11 (nand_11_out, nand_4_out, nand_4_out);
  nand nand_12 (nand_12_out, nand_5_out, nand_5_out);
  nand nand_13 (nand_13_out, nand_11_out, nand_11_out);
  nand nand_14 (nand_14_out, nand_12_out, nand_12_out);
  nand nand_15 (nand_15_out, W, W);
  nand nand_16 (out_5[2], nand_6_out, nand_7_out, nand_8_out);
  nand nand_17 (out_5[1], nand_9_out, nand_10_out);
  nand nand_18 (out_5[3], nand_13_out, nand_14_out, nand_15_out);
  DotMatrix #(.inputtype("row"), .matrixcols(4), .matrixrows(1)) dotmatrix_1 (.row0(out_5));

  // Notes on the sheet:
  //   Md. Rifat Ahmed
  //   ID: 1931725042
endmodule
