// Logisim project Simulation & Circuit 1.circ as structural Verilog: 1 circuit, main circuit main
module main (
  input  W,
  input  X,
  input  Y,
  input  Z,
  output [3:0] out_5
);

  wire and_1_out, and_2_out, and_3_out, and_4_out, and_5_out, and_6_out, and_7_out, not_1_out, not_2_out;

  not not_1 (not_1_out, X);
  not not_2 (not_2_out, Y);
  not not_3 (out_5[0], Z);
  and and_1 (and_1_out, X, Z);
  and and_2 (and_2_out, X, Y);
  and and_3 (and_3_out, not_1_out, Z);
  and and_4 (and_4_out, not_1_out, Y);
  and and_5 (and_5_out, X, not_2_out, out_5[0]);
  and and_6 (and_6_out, not_2_out, out_5[0]);
  and and_7 (and_7_out, Y, Z);
  or or_1 (out_5[3], and_1_out, and_2_out, W);
  or or_2 (out_5[2], and_3_out, and_4_out, and_5_out);
  or or_3 (out_5[1], and_6_out, and_7_out, and_7_out);
  DotMatrix #(.inputtype("row"), .matrixcols(4), .matrixrows(1)) dotmatrix_1 (.row0(out_5));

  // Notes on the sheet:
  //   Md. Rifat Ahmed
  //   ID: 1931725042
endmodule
