// Logisim project Experiment 1 - Adder+Subtractor.circ as structural Verilog: 1 circuit, main circuit main
module main (
  input  [3:0] A,
  input  [3:0] B,
  input  M,
  output out_4,
  output [3:0] out_5
);

  wire [3:0] xor_1_out;

  xor xor_1 (xor_1_out[0], B[0], M);
  xor xor_2 (xor_1_out[1], B[1], M);
  xor xor_3 (xor_1_out[2], B[2], M);
  xor xor_4 (xor_1_out[3], B[3], M);
  Adder #(.width(4)) adder_1 (.a(A), .b(xor_1_out), .out(out_5), .cin(M), .cout(out_4));
  DotMatrix #(.matrixrows(1)) dotmatrix_1 (
    .col0(out_4), .col1(out_5[3]), .col2(out_5[2]), .col3(out_5[1]), .col4(out_5[0]));

  // Notes on the sheet:
  //   Md. Rifat Ahmed
  //   ID: 1931725042
endmodule
