// Logisim project Experiment 2 - Ripple-Through-Carry Adder.circ as structural Verilog: 1 circuit, main circuit main
module main (
  input  [7:0] in_1,
  input  [7:0] in_2,
  input  in_3,
  output out_4,
  output [3:0] out_5,
  output [3:0] out_6
);

  wire adder_1_cout;

  Adder #(.width(4)) adder_1 (.a(in_1[3:0]), .b(in_2[3:0]), .out(out_6), .cin(in_3), .cout(adder_1_cout));
  Adder #(.width(4)) adder_2 (.a(in_1[7:4]), .b(in_2[7:4]), .out(out_5), .cin(adder_1_cout), .cout(out_4));
  DotMatrix #(.matrixcols(9), .matrixrows(1)) dotmatrix_1 (
    .col0(out_4), .col1(out_5[3]), .col2(out_5[2]), .col3(out_5[1]), .col4(out_5[0]), .col5(out_6[3]),
    .col6(out_6[2]), .col7(out_6[1]), .col8(out_6[0]));

  // Notes on the sheet:
  //   Md. Rifat Ahmed
  //   ID: 1931725042
endmodule
