// Logisim project Experiment 3 - BCD Adder.circ as structural Verilog: 1 circuit, main circuit main
module main (
  input  in_1,
  input  [3:0] A,
  input  [3:0] B,
  input  in_4,
  input  in_5,
  output [3:0] out_6
);

  wire adder_1_cout, adder_2_cout, and_1_out, and_2_out, or_2_out;
  wire [2:2] or_1_out;
  wire [3:0] adder_1_out;

  or or_1 (or_1_out[2], adder_1_cout, or_2_out);
  Adder #(.width(4)) adder_1 (.a(A), .b(B), .out(adder_1_out), .cin(in_1), .cout(adder_1_cout));
  or or_2 (or_2_out, and_1_out, and_2_out);
  Adder #(.width(4)) adder_2 (
    .a({in_5, {2{or_1_out[2]}}, in_5}), .b(adder_1_out), .out(out_6), .cin(in_4), .cout(adder_2_cout));
  and and_1 (and_1_out, adder_1_out[3], adder_1_out[1]);
  and and_2 (and_2_out, adder_1_out[3], adder_1_out[2]);
  DotMatrix #(.matrixrows(1)) dotmatrix_1 (
    .col0(adder_2_cout), .col1(out_6[3]), .col2(out_6[2]), .col3(out_6[1]), .col4(out_6[0]));
endmodule
