// Logisim project Exp 1.circ as structural Verilog: 1 circuit, main circuit main
module main (
  input  in_1,
  input  in_2,
  input  [2:0] ABC,
  output out_4
);

  wire not_1_out;

  not not_1 (not_1_out, ABC[2]);
  Multiplexer #(.select(2)) multiplexer_1 (
    .in0(not_1_out), .in1(in_1), .in2(in_2), .in3(ABC[2]), .out(out_4), .sel(ABC[1:0]));  // open: en

  // Notes on the sheet:
  //   Md. Rifat Ahmed
  //   ID: 1931725042
endmodule
