// Logisim project Experiment 2 - JK, T & D using JK.circ as structural Verilog: 1 circuit, main circuit main
module main (
  input  in_1,
  input  in_2,
  input  in_3,
  input  in_4,
  input  in_5,
  input  in_6,
  input  in_7,
  input  in_8,
  input  in_9,
  input  in_10,
  input  in_11,
  input  in_12,
  input  in_13,
  output out_14,
  output out_15,
  output out_16
);

  wire clock_1_out, clock_2_out, clock_3_out, not_1_out;

  Clock clock_1 (.out(clock_1_out));
  Clock clock_2 (.out(clock_2_out));
  J_K_Flip_Flop j_k_ff_1 (
    .J(in_1), .clk(clock_1_out), .K(in_2), .Q(out_14), .preset(in_3), .en(in_4), .reset(in_5));  // open: Qn
  J_K_Flip_Flop T_FF (
    .J(in_6), .clk(clock_2_out), .K(in_6), .Q(out_15), .preset(in_8), .en(in_10), .reset(in_12));  // open: Qn
  not not_1 (not_1_out, in_7);
  Clock clock_3 (.out(clock_3_out));
  J_K_Flip_Flop D_FF (
    .J(in_7), .clk(clock_3_out), .K(not_1_out), .Q(out_16), .preset(in_9), .en(in_11), .reset(in_13));  // open: Qn
endmodule
