// Logisim project Experiment 3.circ as structural Verilog: 1 circuit, main circuit main
module main (
  input  in_1,
  input  in_2,
  input  in_3,
  input  in_4,
  output out_5,
  output out_6,
  output out_7,
  output out_8
);

  wire clock_1_out;

  Clock clock_1 (.out(clock_1_out));
  D_Flip_Flop d_ff_1 (.clk(clock_1_out), .D(in_1), .Q(out_5), .preset(in_2), .en(in_3), .reset(in_4));  // open: Qn
  D_Flip_Flop d_ff_2 (.clk(clock_1_out), .D(out_5), .Q(out_6), .preset(in_2), .en(in_3), .reset(in_4));  // open: Qn
  D_Flip_Flop d_ff_3 (.clk(clock_1_out), .D(out_6), .Q(out_7), .preset(in_2), .en(in_3), .reset(in_4));  // open: Qn
  D_Flip_Flop d_ff_4 (.clk(clock_1_out), .D(out_7), .Q(out_8), .preset(in_2), .en(in_3), .reset(in_4));  // open: Qn

  // Notes on the sheet:
  //   Md. Rifat Ahmed
  //   ID: 1931725042
endmodule
