// Logisim project Experiment 1.circ as structural Verilog: 1 circuit, main circuit main
module main (
  input  X,
  input  in_2,
  input  in_3,
  input  in_4,
  output Y
);

  wire A_qn, and_2_out, clock_1_out, not_1_out;

  not not_1 (not_1_out, X);
  Clock clock_1 (.out(clock_1_out));
  J_K_Flip_Flop B (.J(and_2_out), .clk(clock_1_out), .K(X), .preset(in_2), .en(in_3), .reset(in_4));  // open: Q, Qn
  J_K_Flip_Flop A (.J(X), .clk(clock_1_out), .K(X), .Qn(A_qn), .preset(in_2), .en(in_3), .reset(in_4));  // open: Q
  and and_1 (Y, A_qn, X);
  and and_2 (and_2_out, not_1_out, A_qn);

  // Notes on the sheet:
  //   Md. Rifat Ahmed
  //   ID: 1931725042
endmodule
