// Logisim project Experiment 2.circ as structural Verilog: 1 circuit, main circuit main
module main (
  input  X,
  input  in_2,
  input  in_3,
  input  in_4,
  output Y
);

  wire A_prime_B_prime_X_prime_out, A_qn, B_q, B_qn, BX_out, clock_1_out, not_1_out, or_1_out;

  not not_1 (not_1_out, X);
  Clock clock_1 (.out(clock_1_out));
  and BX (BX_out, B_q, X);
  and A_prime_B_prime_X_prime (A_prime_B_prime_X_prime_out, A_qn, B_qn, not_1_out);
  or or_1 (or_1_out, BX_out, A_prime_B_prime_X_prime_out);
  J_K_Flip_Flop B (
    .J(or_1_out), .clk(clock_1_out), .K(or_1_out), .Q(B_q), .Qn(B_qn), .preset(in_2), .en(in_3), .reset(in_4));
  J_K_Flip_Flop A (.J(X), .clk(clock_1_out), .K(X), .Qn(A_qn), .preset(in_2), .en(in_3), .reset(in_4));  // open: Q
  and A_prime_X (Y, A_qn, X);

  // Notes on the sheet:
  //   Md. Rifat Ahmed
  //   ID: 1931725042
endmodule
