// Logisim project Experiment 3.circ as structural Verilog: 1 circuit, main circuit main
module main (
  input  X,
  input  in_2,
  input  in_3,
  input  in_4,
  output Y
);

  wire A_prime_X_out, A_prime_X_prime_out, A_q, A_qn, AX_prime_out, clock_1_out, not_1_out, or_1_out;

  not not_1 (not_1_out, X);
  Clock clock_1 (.out(clock_1_out));
  and AX_prime (AX_prime_out, A_q, not_1_out);
  and A_prime_X (A_prime_X_out, A_qn, X);
  and A_prime_X_prime (A_prime_X_prime_out, A_qn, not_1_out);
  or or_1 (or_1_out, AX_prime_out, A_prime_X_out);
  D_Flip_Flop B (.clk(clock_1_out), .D(A_prime_X_prime_out), .preset(in_2), .en(in_3), .reset(in_4));  // open: Q, Qn
  D_Flip_Flop A (.clk(clock_1_out), .D(or_1_out), .Q(A_q), .Qn(A_qn), .preset(in_2), .en(in_3), .reset(in_4));
  and A_prime_X_2 (Y, A_qn, X);

  // Notes on the sheet:
  //   Md. Rifat Ahmed
  //   ID: 1931725042
endmodule
